# Fritzing sketch prototype3 (saved by Fritzing 0.9.3b)
circuit board: 6.00893cm x 8.79271cm
breadboards: 2

parts:
  U1 = NodeMCU V1.0
  microSD1 = MicroSD Card Module

nets (from the pcb view):
  N1: U1.D4, microSD1.CS
  GND: U1.GND, microSD1.GND
  N2: U1.D5, microSD1.SCK
  N3: U1.D6, microSD1.MISO
  N4: U1.D7, microSD1.MOSI
  VIN: U1.Vin, microSD1.VCC

notes:
  SDA = D1, SCL=D2
  CS,SCK,MOSI,MISO,VCC,GND
  Analog output
  + D -
  Digital outputs
  D4 and D3
  Treba jos jedan output sa I2C protokolom
  Treba jedan output sa MISO/Mosi protokolom (6channel)
  Digital input
  A0
  D0
  D1
  D2
  D3
  3v3
  GND
  D5
  D6
  D7
  D8
  RX
  TX
  Vin
  I2C
  Display
  SPI
  SD Reader
  CS
  SCK
  MOSI
  MISO
  VCC
  Analog input
  Expert Experiments v3
  SDA
  SCL
  DI/O
  AI

custom parts:
  NodeMCU V1.0: ESP8266 based NodeMCU
